// Digital circuit Async_14Bit_Ripple_Counter.dig as structural Verilog
// Asynchonous 14 Bit ripple counter.
// System clock necessary to set initial state to 0.
module Async_14Bit_Ripple_Counter (
  input  CLOCK,
  input  CLEAR,
  input  SYSTEM_CLOCK,
  output Q_0,
  output Q_1,
  output Q_2,
  output Q_3,
  output Q_4,
  output Q_5,
  output Q_6,
  output Q_7,
  output Q_8,
  output Q_9,
  output Q_10,
  output Q_11,
  output Q_12,
  output Q_13
);

  wire d_ff_as_1_nq, d_ff_as_2_nq, d_ff_as_3_nq, d_ff_as_4_nq, d_ff_as_5_nq, d_ff_as_6_nq, d_ff_as_7_nq,
       d_ff_as_8_nq, d_ff_as_9_nq, d_ff_as_10_nq, d_ff_as_11_nq, d_ff_as_12_nq, d_ff_as_13_nq, d_ff_as_14_nq,
       not_1_out, not_2_out, not_3_out, not_5_out, not_6_out, not_7_out, not_8_out, not_11_out, not_12_out,
       not_13_out, not_14_out, not_17_out, not_18_out, not_19_out, not_20_out, not_23_out, not_24_out,
       not_25_out, not_26_out, not_29_out, not_30_out, not_31_out, not_32_out, not_35_out, not_36_out,
       not_37_out, not_38_out, not_41_out, not_42_out, not_43_out, not_44_out, one_time_fuse_1_y, or_1_out;

  not not_1 (not_1_out, CLOCK);
  not not_2 (not_2_out, CLEAR);
  ONE_TIME_FUSE one_time_fuse_1 (.BLOW(1'b1), .CLOCK(SYSTEM_CLOCK), .y(one_time_fuse_1_y));
  not not_3 (not_3_out, not_2_out);
  or or_1 (or_1_out, not_3_out, one_time_fuse_1_y);
  D_FF_AS d_ff_as_1 (.Set(1'b0), .D(d_ff_as_1_nq), .C(not_1_out), .Clr(or_1_out), .nQ(d_ff_as_1_nq));  // open: Q
  D_FF_AS d_ff_as_2 (.Set(1'b0), .D(d_ff_as_2_nq), .C(d_ff_as_13_nq), .Clr(or_1_out), .nQ(d_ff_as_2_nq));  // open: Q
  not not_4 (Q_0, not_5_out);
  not not_5 (not_5_out, not_6_out);
  not not_6 (not_6_out, d_ff_as_1_nq);
  not not_7 (not_7_out, d_ff_as_2_nq);
  not not_8 (not_8_out, not_7_out);
  not not_9 (Q_7, not_8_out);
  D_FF_AS d_ff_as_3 (.Set(1'b0), .D(d_ff_as_3_nq), .C(d_ff_as_1_nq), .Clr(or_1_out), .nQ(d_ff_as_3_nq));  // open: Q
  D_FF_AS d_ff_as_4 (.Set(1'b0), .D(d_ff_as_4_nq), .C(d_ff_as_2_nq), .Clr(or_1_out), .nQ(d_ff_as_4_nq));  // open: Q
  not not_10 (Q_1, not_11_out);
  not not_11 (not_11_out, not_12_out);
  not not_12 (not_12_out, d_ff_as_3_nq);
  D_FF_AS d_ff_as_5 (.Set(1'b0), .D(d_ff_as_5_nq), .C(d_ff_as_3_nq), .Clr(or_1_out), .nQ(d_ff_as_5_nq));  // open: Q
  D_FF_AS d_ff_as_6 (.Set(1'b0), .D(d_ff_as_6_nq), .C(d_ff_as_4_nq), .Clr(or_1_out), .nQ(d_ff_as_6_nq));  // open: Q
  not not_13 (not_13_out, d_ff_as_4_nq);
  not not_14 (not_14_out, not_13_out);
  not not_15 (Q_8, not_14_out);
  not not_16 (Q_2, not_17_out);
  not not_17 (not_17_out, not_18_out);
  not not_18 (not_18_out, d_ff_as_5_nq);
  not not_19 (not_19_out, d_ff_as_6_nq);
  not not_20 (not_20_out, not_19_out);
  not not_21 (Q_9, not_20_out);
  D_FF_AS d_ff_as_7 (.Set(1'b0), .D(d_ff_as_7_nq), .C(d_ff_as_5_nq), .Clr(or_1_out), .nQ(d_ff_as_7_nq));  // open: Q
  D_FF_AS d_ff_as_8 (.Set(1'b0), .D(d_ff_as_8_nq), .C(d_ff_as_6_nq), .Clr(or_1_out), .nQ(d_ff_as_8_nq));  // open: Q
  not not_22 (Q_3, not_23_out);
  not not_23 (not_23_out, not_24_out);
  not not_24 (not_24_out, d_ff_as_7_nq);
  not not_25 (not_25_out, d_ff_as_8_nq);
  not not_26 (not_26_out, not_25_out);
  not not_27 (Q_10, not_26_out);
  D_FF_AS d_ff_as_9 (.Set(1'b0), .D(d_ff_as_9_nq), .C(d_ff_as_7_nq), .Clr(or_1_out), .nQ(d_ff_as_9_nq));  // open: Q
  D_FF_AS d_ff_as_10 (.Set(1'b0), .D(d_ff_as_10_nq), .C(d_ff_as_8_nq), .Clr(or_1_out), .nQ(d_ff_as_10_nq));  // open: Q
  not not_28 (Q_4, not_29_out);
  not not_29 (not_29_out, not_30_out);
  not not_30 (not_30_out, d_ff_as_9_nq);
  not not_31 (not_31_out, d_ff_as_10_nq);
  not not_32 (not_32_out, not_31_out);
  not not_33 (Q_11, not_32_out);
  D_FF_AS d_ff_as_11 (.Set(1'b0), .D(d_ff_as_11_nq), .C(d_ff_as_9_nq), .Clr(or_1_out), .nQ(d_ff_as_11_nq));  // open: Q
  D_FF_AS d_ff_as_12 (.Set(1'b0), .D(d_ff_as_12_nq), .C(d_ff_as_10_nq), .Clr(or_1_out), .nQ(d_ff_as_12_nq));  // open: Q
  not not_34 (Q_5, not_35_out);
  not not_35 (not_35_out, not_36_out);
  not not_36 (not_36_out, d_ff_as_11_nq);
  D_FF_AS d_ff_as_13 (.Set(1'b0), .D(d_ff_as_13_nq), .C(d_ff_as_11_nq), .Clr(or_1_out), .nQ(d_ff_as_13_nq));  // open: Q
  D_FF_AS d_ff_as_14 (.Set(1'b0), .D(d_ff_as_14_nq), .C(d_ff_as_12_nq), .Clr(or_1_out), .nQ(d_ff_as_14_nq));  // open: Q
  not not_37 (not_37_out, d_ff_as_12_nq);
  not not_38 (not_38_out, not_37_out);
  not not_39 (Q_12, not_38_out);
  not not_40 (Q_6, not_41_out);
  not not_41 (not_41_out, not_42_out);
  not not_42 (not_42_out, d_ff_as_13_nq);
  not not_43 (not_43_out, d_ff_as_14_nq);
  not not_44 (not_44_out, not_43_out);
  not not_45 (Q_13, not_44_out);

  // Notes on the sheet:
  //   SYSTEM_CLOCK: Hz: 2147483647
endmodule
