// Digital circuit Control_Unit.dig as structural Verilog
module Control_Unit (
  input  x_1,
  input  x_0,
  input  CLOCK,
  output Q_1,
  output Q_0
);

  wire and_1_out, and_2_out, and_3_out, and_4_out, or_1_out, or_2_out, z_1_nq;

  and and_1 (and_1_out, ~x_1, Q_0);  // And
  and and_2 (and_2_out, Q_0, x_0);
  and and_3 (and_3_out, z_1_nq, ~x_0);  // And
  or or_1 (or_1_out, ~x_1, x_0);  // Or
  or or_2 (or_2_out, and_1_out, and_2_out);
  and and_4 (and_4_out, and_3_out, x_1);
  JK_FF z_1 (.J(or_2_out), .C(CLOCK), .K(Q_1), .Q(Q_1), .nQ(z_1_nq));
  JK_FF z_0 (.J(and_4_out), .C(CLOCK), .K(or_1_out), .Q(Q_0));  // open: nQ
endmodule
