// Digital circuit Main.dig as structural Verilog
module Main (
  input  SYSTEM_CLOCK,
  output RESET,
  output MOTOR,
  output x_0,
  output x_1
);

  wire async_14bit_ripple_counter_1_q0, async_14bit_ripple_counter_1_q1, async_14bit_ripple_counter_1_q2,
       async_14bit_ripple_counter_1_q3, async_14bit_ripple_counter_1_q4, async_14bit_ripple_counter_1_q5,
       async_14bit_ripple_counter_1_q6, async_14bit_ripple_counter_1_q7, async_14bit_ripple_counter_1_q8,
       async_14bit_ripple_counter_1_q9, async_14bit_ripple_counter_1_q10, async_14bit_ripple_counter_1_q11,
       async_14bit_ripple_counter_1_q12, async_14bit_ripple_counter_1_q13, async_14bit_ripple_counter_2_q0,
       async_14bit_ripple_counter_2_q1, async_14bit_ripple_counter_2_q2, async_14bit_ripple_counter_2_q3,
       async_14bit_ripple_counter_2_q4, async_14bit_ripple_counter_2_q5, async_14bit_ripple_counter_2_q6,
       async_14bit_ripple_counter_2_q7, async_14bit_ripple_counter_2_q8, async_14bit_ripple_counter_2_q9,
       async_14bit_ripple_counter_2_q10, async_14bit_ripple_counter_2_q11, async_14bit_ripple_counter_2_q12,
       jk_ff_3_q, multiplexer_1_out, multiplexer_2_out, not_1_out, sel0, sel0_out, sel1, sel1_out,
       switchdt_1_p2;

  Button u_sel1 (.out(sel1_out));
  Button u_sel0 (.out(sel0_out));
  Async_14Bit_Ripple_Counter async_14bit_ripple_counter_1 (
    .CLOCK(SYSTEM_CLOCK), .CLEAR(RESET), .SYSTEM_CLOCK(SYSTEM_CLOCK), .Q0(async_14bit_ripple_counter_1_q0),
    .Q1(async_14bit_ripple_counter_1_q1), .Q2(async_14bit_ripple_counter_1_q2),
    .Q3(async_14bit_ripple_counter_1_q3), .Q4(async_14bit_ripple_counter_1_q4),
    .Q5(async_14bit_ripple_counter_1_q5), .Q6(async_14bit_ripple_counter_1_q6),
    .Q7(async_14bit_ripple_counter_1_q7), .Q8(async_14bit_ripple_counter_1_q8),
    .Q9(async_14bit_ripple_counter_1_q9), .Q10(async_14bit_ripple_counter_1_q10),
    .Q11(async_14bit_ripple_counter_1_q11), .Q12(async_14bit_ripple_counter_1_q12),
    .Q13(async_14bit_ripple_counter_1_q13));
  JK_FF jk_ff_1 (.J(1'b1), .C(sel1_out), .K(1'b1), .Q(sel1));  // open: nQ
  JK_FF jk_ff_2 (.J(1'b1), .C(sel0_out), .K(1'b1), .Q(sel0));  // open: nQ
  // Probe on async_14bit_ripple_counter_1_q0
  // Probe on async_14bit_ripple_counter_1_q1
  // Probe on async_14bit_ripple_counter_1_q2
  // Probe on async_14bit_ripple_counter_1_q3
  // Probe on async_14bit_ripple_counter_1_q4
  // Probe on async_14bit_ripple_counter_1_q5
  // Probe on async_14bit_ripple_counter_1_q6
  // Probe on async_14bit_ripple_counter_1_q7
  // Probe on async_14bit_ripple_counter_1_q8
  // Probe on async_14bit_ripple_counter_1_q9
  // Probe on async_14bit_ripple_counter_1_q10
  // Probe on async_14bit_ripple_counter_1_q11
  // Probe on async_14bit_ripple_counter_1_q12
  // Probe on async_14bit_ripple_counter_1_q13
  JK_FF jk_ff_3 (.J(1'b1), .C(async_14bit_ripple_counter_1_q13), .K(1'b1), .Q(jk_ff_3_q));  // open: nQ
  not not_1 (not_1_out, RESET);
  // SwitchDT switchdt_1: pin names not known; wires that end beside it: jk_ff_3_q, switchdt_1_p2
  Break break_1 (.brk(not_1_out));
  Async_14Bit_Ripple_Counter async_14bit_ripple_counter_2 (
    .CLOCK(switchdt_1_p2), .CLEAR(RESET), .SYSTEM_CLOCK(SYSTEM_CLOCK), .Q0(async_14bit_ripple_counter_2_q0),
    .Q1(async_14bit_ripple_counter_2_q1), .Q2(async_14bit_ripple_counter_2_q2),
    .Q3(async_14bit_ripple_counter_2_q3), .Q4(async_14bit_ripple_counter_2_q4),
    .Q5(async_14bit_ripple_counter_2_q5), .Q6(async_14bit_ripple_counter_2_q6),
    .Q7(async_14bit_ripple_counter_2_q7), .Q8(async_14bit_ripple_counter_2_q8),
    .Q9(async_14bit_ripple_counter_2_q9), .Q10(async_14bit_ripple_counter_2_q10),
    .Q11(async_14bit_ripple_counter_2_q11), .Q12(async_14bit_ripple_counter_2_q12), .Q13(x_1));
  // Probe on async_14bit_ripple_counter_2_q0
  // Probe on async_14bit_ripple_counter_2_q1
  // Probe on async_14bit_ripple_counter_2_q2
  // Probe on async_14bit_ripple_counter_2_q3
  // Probe on async_14bit_ripple_counter_2_q8
  // Probe on async_14bit_ripple_counter_2_q9
  // Probe on async_14bit_ripple_counter_2_q10
  // Probe on async_14bit_ripple_counter_2_q11
  // Probe on async_14bit_ripple_counter_2_q12
  // Probe on x_1
  Multiplexer multiplexer_1 (
    .sel(sel1), .in_0(async_14bit_ripple_counter_2_q4), .in_1(async_14bit_ripple_counter_2_q5),
    .out(multiplexer_1_out));
  Multiplexer multiplexer_2 (
    .sel(sel1), .in_0(async_14bit_ripple_counter_2_q6), .in_1(async_14bit_ripple_counter_2_q7),
    .out(multiplexer_2_out));
  Multiplexer multiplexer_3 (.sel(sel0), .in_0(multiplexer_1_out), .in_1(multiplexer_2_out), .out(x_0));
  Control_Unit control_unit_1 (.x1(x_1), .x0(x_0), .CLOCK(SYSTEM_CLOCK), .y1(RESET), .y0(MOTOR));
  Break RESET_BREAK (.brk(RESET));
  Break MOTOR_BREAK (.brk(MOTOR));

  // Other names for the same wires on the sheet: SYS_CLK = SYSTEM_CLOCK

  // Notes on the sheet:
  //   SYSTEM_CLOCK: Hz: 32768
endmodule
