// Digital circuit 1_MUX.dig as structural Verilog
module _1_MUX (
  input  a,
  input  sel,
  input  b,
  output y
);

  wire nand_1_out, nand_2_out, nand_3_out;

  nand nand_1 (nand_1_out, sel, sel);
  nand nand_2 (nand_2_out, a, nand_1_out);
  nand nand_3 (nand_3_out, sel, b);
  nand nand_4 (y, nand_2_out, nand_3_out);
endmodule
