// Digital circuit ONE_TIME_FUSE.dig as structural Verilog
module ONE_TIME_FUSE (
  input  BLOW,
  input  CLOCK,
  output y
);

  wire and_1_out, z1n;

  and and_1 (and_1_out, z1n, BLOW);
  JK_FF z1 (.J(y), .C(CLOCK), .K(1'b0), .nQ(z1n));  // open: Q
  JK_FF z0 (.J(and_1_out), .C(CLOCK), .K(y), .Q(y));  // open: nQ
endmodule
