// Digital circuit Test.dig as structural Verilog
module Test (
  input  CLK,
  input  in_2,
  input  _8H,
  output RESET,
  output MOTOR
);

  wire and_1_out, and_2_out, and_3_out, and_4_out, button_1_out, button_2_out, jk_ff_1_q, jk_ff_2_q,
       multiplexer_1_out, multiplexer_2_out, multiplexer_3_out, nand_1_out, t_ff_1_q, t_ff_2_q, t_ff_3_q,
       t_ff_4_q, t_ff_5_q, t_ff_6_q, t_ff_7_q, t_ff_8_q, z1_nq;

  and and_1 (and_1_out, in_2, CLK);
  T_FF t_ff_1 (.T(1'b1), .C(and_1_out), .Q(t_ff_1_q));  // open: nQ
  Button button_1 (.out(button_1_out));
  Button button_2 (.out(button_2_out));
  T_FF t_ff_2 (.T(1'b1), .C(t_ff_1_q), .Q(t_ff_2_q));  // open: nQ
  JK_FF jk_ff_1 (.J(1'b1), .C(button_1_out), .K(1'b1), .Q(jk_ff_1_q));  // open: nQ
  JK_FF jk_ff_2 (.J(1'b1), .C(button_2_out), .K(1'b1), .Q(jk_ff_2_q));  // open: nQ
  T_FF t_ff_3 (.T(1'b1), .C(t_ff_2_q), .Q(t_ff_3_q));  // open: nQ
  T_FF t_ff_4 (.T(1'b1), .C(t_ff_3_q), .Q(t_ff_4_q));  // open: nQ
  Multiplexer multiplexer_1 (.sel(jk_ff_1_q), .in_0(t_ff_8_q), .in_1(t_ff_7_q), .out(multiplexer_1_out));
  Multiplexer multiplexer_2 (.sel(jk_ff_1_q), .in_0(t_ff_6_q), .in_1(t_ff_5_q), .out(multiplexer_2_out));
  Multiplexer multiplexer_3 (
    .sel(jk_ff_2_q), .in_0(multiplexer_1_out), .in_1(multiplexer_2_out), .out(multiplexer_3_out));
  T_FF t_ff_5 (.T(1'b1), .C(t_ff_4_q), .Q(t_ff_5_q));  // open: nQ
  nand nand_1 (nand_1_out, multiplexer_3_out, _8H);
  and and_2 (and_2_out, multiplexer_3_out, _8H);
  T_FF t_ff_6 (.T(1'b1), .C(t_ff_5_q), .Q(t_ff_6_q));  // open: nQ
  and and_3 (and_3_out, and_2_out, z1_nq);
  and and_4 (and_4_out, nand_1_out, MOTOR);
  T_FF t_ff_7 (.T(1'b1), .C(t_ff_6_q), .Q(t_ff_7_q));  // open: nQ
  JK_FF z1 (.J(and_4_out), .C(~CLK), .K(RESET), .Q(RESET), .nQ(z1_nq));
  JK_FF z0 (.J(and_3_out), .C(~CLK), .K(and_4_out), .Q(MOTOR));  // open: nQ
  T_FF t_ff_8 (.T(1'b1), .C(t_ff_7_q), .Q(t_ff_8_q));  // open: nQ

  // Notes on the sheet:
  //   CLK: Hz: 50
endmodule
